# Fritzing sketch circuitDiagram (saved by Fritzing 0.9.9b)
circuit board: 8.46667cm x 5.64444cm

parts:
  U1 = ESP32-38PinWide [part_number=ESP32-38PinWide]
  Bauteil4 = Adafruit MAX98357A I2S 3W Class D Amplifier [part_number="Adafruit #3006"]
  Bauteil6 = Adafruit MAX98357A I2S 3W Class D Amplifier [part_number="Adafruit #3006"]
  Bauteil2 = Adafruit MAX98357A I2S 3W Class D Amplifier [part_number="Adafruit #3006"]  # not connected
  Bauteil4_2 = Adafruit MAX98357A I2S 3W Class D Amplifier [part_number="Adafruit #3006"]
  Bauteil3 = Adafruit MAX98357A I2S 3W Class D Amplifier [part_number="Adafruit #3006"]
  Bauteil5 = Adafruit MAX98357A I2S 3W Class D Amplifier [part_number="Adafruit #3006"]  # not connected
  R2 = Resistor [tolerance=±5% resistance=0 package="2512 [SMD]"]  # not connected
  R3 = Resistor [tolerance=±5% resistance=0 package="2512 [SMD]"]  # not connected

nets:
  N1: U1.GPIO35, Bauteil6.DIN
  N2: U1.GPIO32, Bauteil3.DIN
  N3: U1.GPIO33, Bauteil4_2.DIN
  N4: U1.GPIO25, Bauteil6.BCLK
  N5: U1.GPIO26, Bauteil6.LRCLK
  GND: U1.GND, Bauteil6.GND
  5V: U1.VIN, Bauteil6.VIN
  GND_2: Bauteil4.GND, Bauteil3.GND

notes:
  Coil 1
  Coil 2
  Coil 3
  Coil 4
  Coil 5
  Coil 6
  Coil I/O

custom parts:
  ESP32-38PinWide: Generic 38-Pin ESP32 with wide format (only access to one side of pins on a breadboard) based on Stephen Lilley's HiLetgo ESP-WROOM-32 ESP32 ESP-32S Development Board.
  Adafruit MAX98357A I2S 3W Class D Amplifier: Listen to this good news - we now have an all in one digital audio amp breakout board that works incredibly well with the Raspberry Pi! If you're looking for an easy and low cost way to get you digital sound files bumpin' then the MAX08357 I2S Amp Breakout is for you. It takes standard I2S digital audio input and, not only decodes it into analog, but also amplifies it directly into a speaker.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
